# Fritzing sketch WifiEnergyMonitorFerraris8266 (saved by Fritzing 0.9.3b)
stripboards: 1

parts:
  R1 = Resistor [tolerance=±1% resistance=10k package=THT]
  R2 = Resistor [tolerance=±1% resistance=5k package=THT]
  C1 = Ceramic Capacitor [capacitance=100nF package="100 mil [THT, multilayer]"]  # not connected
  U1 = NodeMCU V1.0
  R3 = Resistor [tolerance=±1% resistance=1k package=THT]
  R4 = Resistor [tolerance=±1% resistance=1k package=THT]

nets:
  N1: R1.Pin_0, R2.Pin_1, U1.A0
  N2: R1.Pin_1, U1.GND
  N3: U1.D1, R3.Pin_1
  N4: U1.D2, R4.Pin_1

custom parts:
  NodeMCU V1.0: ESP8266 based NodeMCU
